// Logisim project branch_comp.circ as structural Verilog: 1 circuit, main circuit branch_comp
module branch_comp (
  input  [31:0] inst,
  input  [31:0] ximm,
  input  [31:0] pc,
  input  zero,
  input  [1:0] BrUn,
  output [31:0] newPC,
  output BrJmp
);

  wire comparator_1_eq, comparator_2_eq, comparator_3_eq, comparator_4_eq;
  wire [27:0] bit_extender_1_out, shifter_3_out;
  wire [31:0] adder_1_out, adder_2_out, adder_3_out, adder_4_out, adder_5_out, and_1_out, bit_extender_2_out,
       Brunch, Jump, shifter_1_out, shifter_2_out;

  Adder #(.width(32)) adder_1 (.a(pc), .b(32'h4), .out(adder_1_out));  // open: cin, cout
  Adder #(.width(32)) adder_2 (.a(pc), .b(32'h4), .out(adder_2_out));  // open: cin, cout
  Shifter #(.width(32)) shifter_1 (.in(ximm), .\dist (5'b00010), .out(shifter_1_out));
  Adder #(.width(32)) adder_3 (.a(pc), .b(32'h4), .out(adder_3_out));  // open: cin, cout
  Shifter #(.width(32)) shifter_2 (.in(ximm), .\dist (5'b00010), .out(shifter_2_out));
  assign bit_extender_1_out = {{2{1'b0}}, inst[25:0]};  // Bit_Extender bit_extender_1
  assign and_1_out = 32'hf0000000 & adder_1_out;  // AND_Gate and_1, 32 bits wide
  Adder #(.width(32)) adder_4 (.a(adder_2_out), .b(shifter_1_out), .out(adder_4_out));  // open: cin, cout
  Adder #(.width(32)) adder_5 (.a(adder_3_out), .b(shifter_2_out), .out(adder_5_out));  // open: cin, cout
  assign bit_extender_2_out = {{4{1'b0}}, shifter_3_out};  // Bit_Extender bit_extender_2
  Shifter #(.width(28)) shifter_3 (.in(bit_extender_1_out), .\dist (5'b00010), .out(shifter_3_out));
  Multiplexer #(.enable("false"), .width(32)) multiplexer_1 (
    .in0(adder_4_out), .in1(adder_5_out), .out(Brunch), .sel(zero));
  assign Jump = bit_extender_2_out | and_1_out;  // OR_Gate or_1, 32 bits wide
  Multiplexer #(.enable("false"), .select(2), .width(32)) multiplexer_2 (
    .in0({32{1'b0}}), .in1(Brunch), .in2(Jump), .out(newPC), .sel(BrUn));  // open: in3
  Comparator #(.mode("unsigned"), .width(6)) comparator_1 (
    .a(inst[31:26]), .b(6'b000010), .eq(comparator_1_eq));  // open: gt, lt
  Comparator #(.mode("unsigned"), .width(6)) comparator_2 (
    .a(inst[31:26]), .b(6'b000011), .eq(comparator_2_eq));  // open: gt, lt
  Comparator #(.mode("unsigned"), .width(6)) comparator_3 (
    .a(inst[31:26]), .b(6'b000100), .eq(comparator_3_eq));  // open: gt, lt
  Comparator #(.mode("unsigned"), .width(6)) comparator_4 (
    .a(inst[31:26]), .b(6'b000101), .eq(comparator_4_eq));  // open: gt, lt
  or or_2 (BrJmp, comparator_1_eq, comparator_2_eq, comparator_3_eq, comparator_4_eq);

  // Notes on the sheet:
  //   ENTREES de votre circuit
  //   NE CHANGEZ PAS LES EMPLACEMENTS DES ENTRÉES ET DES SORTIES !
  //   SORTIES de votre circuit
endmodule
