// Logisim project cpu_pipelined.circ as structural Verilog: 1 circuit, main circuit cpu
module cpu (
  input  clk,
  input  [31:0] INSTRUCTION,
  input  [31:0] READ_DATA,
  output [31:0] DMEM_ADDRESS,
  output [31:0] IMEM_ADDRESS,
  output [31:0] ra,
  output [31:0] sp,
  output [31:0] t0,
  output [31:0] t1,
  output [31:0] t2,
  output [31:0] s0,
  output [31:0] s1,
  output [31:0] a0,
  output [3:0] WRITE_ENABLE,
  output [31:0] WRITE_DATA
);

  wire ASel, BrJmp, MemRW, or_1_out, or_2_out, PCSel, RegWEn, zero;
  wire [1:0] Brun, BSel, control_logic_1_p6, MemSel, RegWSel, WBSel;
  wire [3:0] ALUSel;
  wire [4:0] multiplexer_2_out, rd, rs, rt, shmt;
  wire [5:0] Func, opcode;
  wire [31:0] bit_extender_1_out, data1, data2, imm, INSTRUCTION_t, multiplexer_1_out, multiplexer_3_out,
       multiplexer_4_out, multiplexer_6_out, NewPC, pc, pc4, regfile_1_p4;

  Multiplexer #(.enable("false"), .width(32)) multiplexer_1 (
    .in0(INSTRUCTION), .in1({32{1'b0}}), .out(multiplexer_1_out), .sel(or_1_out));
  or or_1 (or_1_out, BrJmp, PCSel);
  Register #(.width(32)) u_PC (.D(pc), .clk(clk), .Q(IMEM_ADDRESS));  // open: en, clr
  Adder #(.width(32)) adder_1 (.a(32'h4), .b(IMEM_ADDRESS), .out(pc4));  // open: cin, cout
  Register #(.width(32)) register_1 (
    .D(multiplexer_1_out), .en(1'b1), .clk(clk), .Q({opcode, rs, rt, rd, shmt, Func}));  // open: clr
  Multiplexer #(.enable("false"), .select(2), .width(5)) multiplexer_2 (
    .in0(rd), .in1(rt), .in2({5{1'b1}}), .out(multiplexer_2_out), .sel(RegWSel));  // open: in3
  or or_2 (or_2_out, RegWEn, MemRW);
  // control_logic control_logic_1: pin names not known; wires that end beside it: opcode, Func, PCSel, RegWSel, RegWEn, control_logic_1_p6, Brun
  branch_comp branch_comp_1 (
    .inst(INSTRUCTION_t), .ximm(imm), .pc(IMEM_ADDRESS), .zero(zero), .BrUn(Brun), .newPC(NewPC),
    .BrJmp(BrJmp));
  // regfile regfile_1: pin names not known; wires that end beside it: rs, rt, multiplexer_2_out, regfile_1_p4, or_2_out, clk, ra, sp, t0, t1, t2, s0, s1, a0, data1, data2
  imm_gen imm_gen_1 (.inst({opcode, rs, rt, rd, shmt, Func}), .ImmSel(control_logic_1_p6), .Imm(imm));
  assign bit_extender_1_out = {{27{1'b0}}, shmt};  // Bit_Extender bit_extender_1
  Multiplexer #(.enable("false"), .width(32)) multiplexer_3 (
    .in0(data1), .in1(data2), .out(multiplexer_3_out), .sel(ASel));
  Multiplexer #(.enable("false"), .select(2), .width(32)) multiplexer_4 (
    .in0(data2), .in1(imm), .in2(bit_extender_1_out), .in3(data1), .out(multiplexer_4_out), .sel(BSel));
  // alu alu_1: pin names not known; wires that end beside it: multiplexer_3_out, multiplexer_4_out, zero, ALUSel, DMEM_ADDRESS
  Multiplexer #(.enable("false"), .select(2), .width(32)) multiplexer_5 (
    .in0(DMEM_ADDRESS), .in1(READ_DATA), .in2(IMEM_ADDRESS), .in3(imm), .out(regfile_1_p4), .sel(WBSel));
  Multiplexer #(.enable("false"), .width(32)) multiplexer_6 (
    .in0(pc4), .in1(NewPC), .out(multiplexer_6_out), .sel(BrJmp));
  Multiplexer #(.enable("false"), .width(32)) multiplexer_7 (
    .in0(multiplexer_6_out), .in1(data1), .out(pc), .sel(PCSel));
  Multiplexer #(.enable("false"), .select(2), .width(4)) multiplexer_8 (
    .in0(4'b0000), .in1(4'b0001), .in2(4'b0010), .in3(4'b0100), .out(WRITE_ENABLE), .sel(MemSel));

  assign WRITE_DATA = DMEM_ADDRESS;

  // Other names for the same wires on the sheet: INST_PP[31:0] = INSTRUCTION; result[31:0] = DMEM_ADDRESS

  // Notes on the sheet:
  //   Output to IMEM
  //   IMEM (ne **PAS** déplacer ceci)
  //   Inputs from IMEM
  //   Vous pouvez déplacer le PC, RegFile, ALU, MEM, Branch Comp, Imm Gen et Control Logic à l'endroit qui vous convient le mieux lors de la construction de votre CPU, et supprimer ce texte
  //   Entrées / sorties pour les tests. Ne les déplacez **PAS**.
  //   Outputs To DMEM
  //   DMEM (ne **PAS** déplacer ceci)
  //   Inputs From DMEM
endmodule
