// Logisim project cpu_single.circ as structural Verilog: 1 circuit, main circuit cpu
module cpu (
  input  clk,
  input  [31:0] INSTRUCTION,
  input  [31:0] READ_DATA,
  output [31:0] DMEM_ADDRESS,
  output [31:0] IMEM_ADDRESS,
  output [31:0] ra,
  output [31:0] sp,
  output [31:0] t0,
  output [31:0] t1,
  output [31:0] t2,
  output [31:0] s0,
  output [31:0] s1,
  output [31:0] a0,
  output [3:0] WRITE_ENABLE,
  output [31:0] WRITE_DATA
);

  wire ASel, BrJmp, comparator_1_eq, comparator_2_eq, comparator_3_eq, MemRW, or_1_out, PCSel, RegWen, zero;
  wire [1:0] Brun, BSel, control_logic_1_p6, MemSel, RegWSel, WBSel;
  wire [3:0] ALUSel;
  wire [4:0] multiplexer_3_out;
  wire [5:0] or_2_out, or_3_out, or_4_out;
  wire [31:0] adder_1_out, adder_2_out, bit_extender_1_out, data1, imm, multiplexer_1_out, multiplexer_2_out,
       multiplexer_4_out, multiplexer_5_out, multiplexer_7_out, multiplexer_9_out, NewPC, regfile_1_p4,
       result, shifter_1_out, shifter_2_out;

  Multiplexer #(.enable("false"), .width(32)) multiplexer_1 (
    .in0(adder_1_out), .in1(NewPC), .out(multiplexer_1_out), .sel(BrJmp));
  Register #(.width(32)) PC (.D(multiplexer_2_out), .clk(clk), .Q(IMEM_ADDRESS));  // open: en, clr
  Multiplexer #(.enable("false"), .width(32)) multiplexer_2 (
    .in0(multiplexer_1_out), .in1(data1), .out(multiplexer_2_out), .sel(PCSel));
  Adder #(.width(32)) adder_1 (.a(32'h4), .b(IMEM_ADDRESS), .out(adder_1_out));  // open: cin, cout
  // control_logic control_logic_1: pin names not known; wires that end beside it: INSTRUCTION[31:26], INSTRUCTION[5:0], PCSel, RegWSel, RegWen, control_logic_1_p6, Brun
  Multiplexer #(.enable("false"), .select(2), .width(5)) multiplexer_3 (
    .in0(INSTRUCTION[15:11]), .in1(INSTRUCTION[20:16]), .in2({5{1'b1}}), .out(multiplexer_3_out),
    .sel(RegWSel));  // open: in3
  or or_1 (or_1_out, RegWen, MemRW);
  branch_comp branch_comp_1 (
    .inst(INSTRUCTION), .ximm(imm), .pc(IMEM_ADDRESS), .zero(zero), .BrUn(Brun), .newPC(NewPC), .BrJmp(BrJmp));
  // regfile regfile_1: pin names not known; wires that end beside it: INSTRUCTION[25:21], INSTRUCTION[20:16], multiplexer_3_out, regfile_1_p4, or_1_out, clk, ra, sp, t0, t1, t2, s0, s1, a0, data1, WRITE_DATA
  imm_gen imm_gen_1 (.inst(INSTRUCTION), .ImmSel(control_logic_1_p6), .Imm(imm));
  assign bit_extender_1_out = {{27{1'b0}}, INSTRUCTION[10:6]};  // Bit_Extender bit_extender_1
  Multiplexer #(.enable("false"), .width(32)) multiplexer_4 (
    .in0(data1), .in1(WRITE_DATA), .out(multiplexer_4_out), .sel(ASel));
  Multiplexer #(.enable("false"), .select(2), .width(32)) multiplexer_5 (
    .in0(WRITE_DATA), .in1(imm), .in2(bit_extender_1_out), .in3(data1), .out(multiplexer_5_out), .sel(BSel));
  Multiplexer #(.enable("false"), .select(2), .width(32)) multiplexer_6 (
    .in0(result), .in1(READ_DATA), .in2(adder_2_out), .in3(imm), .out(regfile_1_p4), .sel(WBSel));
  Adder #(.width(32)) adder_2 (.a(32'h4), .b(IMEM_ADDRESS), .out(adder_2_out));  // open: cin, cout
  // alu alu_1: pin names not known; wires that end beside it: multiplexer_4_out, multiplexer_5_out, zero, ALUSel, result
  assign or_2_out = 6'b100000 | 6'b101000;  // OR_Gate or_2, 6 bits wide
  Comparator #(.mode("unsigned"), .width(6)) comparator_1 (
    .a(INSTRUCTION[31:26]), .b(or_2_out), .eq(comparator_1_eq));  // open: gt, lt
  Multiplexer #(.enable("false"), .width(32)) multiplexer_7 (
    .in0({32{1'b0}}), .in1(result), .out(multiplexer_7_out), .sel(comparator_1_eq));
  Multiplexer #(.enable("false"), .select(2), .width(4)) multiplexer_8 (
    .in0(4'b0000), .in1(4'b0001), .in2(4'b0010), .in3(4'b0100), .out(WRITE_ENABLE), .sel(MemSel));
  Shifter #(.width(32)) shifter_1 (.in(result), .\dist (5'b00001), .out(shifter_1_out));
  Comparator #(.mode("unsigned"), .width(6)) comparator_2 (
    .a(INSTRUCTION[31:26]), .b(or_3_out), .eq(comparator_2_eq));  // open: gt, lt
  assign or_3_out = 6'b100001 | 6'b101001;  // OR_Gate or_3, 6 bits wide
  Multiplexer #(.enable("false"), .width(32)) multiplexer_9 (
    .in0(multiplexer_7_out), .in1(shifter_1_out), .out(multiplexer_9_out), .sel(comparator_2_eq));
  Shifter #(.width(32)) shifter_2 (.in(result), .\dist (5'b00010), .out(shifter_2_out));
  assign or_4_out = 6'b100011 | 6'b101011;  // OR_Gate or_4, 6 bits wide
  Comparator #(.mode("unsigned"), .width(6)) comparator_3 (
    .a(INSTRUCTION[31:26]), .b(or_4_out), .eq(comparator_3_eq));  // open: gt, lt
  Multiplexer #(.enable("false"), .width(32)) multiplexer_10 (
    .in0(multiplexer_9_out), .in1(shifter_2_out), .out(DMEM_ADDRESS), .sel(comparator_3_eq));

  // Other names for the same wires on the sheet: data2[31:0] = WRITE_DATA; Func[5:0] = INSTRUCTION[5:0];
  //   shmt[4:0] = INSTRUCTION[10:6]; rd[4:0] = INSTRUCTION[15:11]; rt[4:0] = INSTRUCTION[20:16];
  //   rs[4:0] = INSTRUCTION[25:21]; opcode[5:0] = INSTRUCTION[31:26]

  // Notes on the sheet:
  //   Output to IMEM
  //   IMEM (ne **PAS** déplacer ceci)
  //   Inputs from IMEM
  //   Vous pouvez déplacer le PC, RegFile, ALU, MEM, Branch Comp, Imm Gen et Control Logic à l'endroit qui vous convient le mieux lors de la construction de votre CPU, et supprimer ce texte
  //   Entrées / sorties pour les tests. Ne les déplacez **PAS**.
  //   Outputs To DMEM
  //   DMEM (ne **PAS** déplacer ceci)
  //   Inputs From DMEM
endmodule
