// Logisim project imm_gen.circ as structural Verilog: 1 circuit, main circuit imm_gen
module imm_gen (
  input  [31:0] inst,
  input  [1:0] ImmSel,
  output [31:0] Imm
);

  wire [31:0] bit_extender_3_out, i0_imm, i_imm, lui_imm;

  assign i_imm = {{16{inst[15]}}, inst[15:0]};  // Bit_Extender bit_extender_1
  assign i0_imm = {{16{1'b0}}, inst[15:0]};  // Bit_Extender bit_extender_2
  assign bit_extender_3_out = {{16{1'b0}}, inst[15:0]};  // Bit_Extender bit_extender_3
  Shifter #(.width(32)) shifter_1 (.in(bit_extender_3_out), .\dist (5'b10000), .out(lui_imm));
  Multiplexer #(.enable("false"), .select(2), .width(32)) multiplexer_1 (
    .in0({32{1'b0}}), .in1(i_imm), .in2(i0_imm), .in3(lui_imm), .out(Imm), .sel(ImmSel));

  // Notes on the sheet:
  //   ENTREES pour votre circuit
  //   NE CHANGEZ PAS LES EMPLACEMENTS DES ENTRÉES ET DES SORTIES!
  //   SORTIE de votre circuit
endmodule
